# Fritzing sketch GPS_Client_PICO (saved by Fritzing 1.0.1rc)
circuit board: 8.46667cm x 5.64444cm
breadboards: 1

parts:
  Nokia_5110_LCD_Module2 = Nokia 5110 LCD basado en PCD8544
  Mod2 = Raspberry Pi Pico W
  A2 = GY-NEO6MV2
  Sensor1 = TTP223B Capacitive Touch Sensor Module
  U2 = LIPO-2000mAh [package=lipo-2000]

nets:
  N1: Nokia_5110_LCD_Module2.VCC, Mod2.pin_36
  GND: Nokia_5110_LCD_Module2.GND, A2.Tx, Sensor1.GND, U2.-
  N2: Nokia_5110_LCD_Module2.CE, Mod2.pin_22
  N3: Nokia_5110_LCD_Module2.RST, Mod2.pin_27
  N4: Nokia_5110_LCD_Module2.DC, Mod2.pin_26
  N5: Nokia_5110_LCD_Module2.DIN, Mod2.pin_25
  N6: Nokia_5110_LCD_Module2.CLK, Mod2.pin_24
  N7: Mod2.pin_1, A2.Vcc#1
  N8: Mod2.pin_2, A2.Rx
  N9: Mod2.pin_3, Mod2.pin_8, Mod2.pin_13, Mod2.pin_18, Mod2.pin_23, Mod2.pin_28, Mod2.pin_33, Mod2.pin_38
  N10: Mod2.pin_21, Mod2.pin_39, A2.Vcc#0, Sensor1.VCC, Sensor1.SIG, U2.+

custom parts:
  Nokia 5110 LCD basado en PCD8544: Módulo Nokia 5110 LCD basado en el controlador PCD8544. Versión de 8 pines (sólo entrada).
  Raspberry Pi Pico W: Raspberry Pi Pico W. Based around the RP2040 microcontroller the Pico W is a low cost microcontroller device bringing Raspberry Pi quality, cost, and easy of use to the microcontroller space. The areas marked KEEPOUT in pcb silkscreen should not have traces running through them to avoid shorts on a soldered in module!
  GY-NEO6MV2: Description: Module GPS , type GY-NEO6MV2, pour arduino et autres micro-contrôleurs. Caractéristiques De type GY-NEO6MV2 Alimentation 3V-5V Avec Flight Control EEPROM MWC Antenne large céramique, fort signal, 25 x 25 mm Paramètres de configuration sauvegardés en EEPROM Avec batterie de backup de données LED témoin de signal Module miniaturisé 25 x 35 mm Trou de fixation de 3mm Baud rate par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
  TTP223B Capacitive Touch Sensor Module: The TTP223B capacitive touch sensor module uses the TTP223B IC. The appropriate voltage is approximately 2 to 5.5 volts.
