# Fritzing sketch GPS_Client_RP2040_Zero (saved by Fritzing 0.9.6b)
circuit board: 8.46667cm x 5.64444cm
breadboards: 1

parts:
  Nokia_5110_LCD_Module2 = Nokia 5110 LCD basado en PCD8544
  A2 = GY-NEO6MV2
  A3 = Waveshare rp2040-zero tht [package=THT]
  Sensor1 = TTP223B Capacitive Touch Sensor Module
  U1 = LIPO-2000mAh [package=lipo-2000]

nets:
  N1: Nokia_5110_LCD_Module2.VCC, A3.Pin_3
  GND: Nokia_5110_LCD_Module2.GND, A2.Tx, A3.Pin_2, Sensor1.GND, U1.-
  N2: Nokia_5110_LCD_Module2.CE, A3.Pin_18
  N3: Nokia_5110_LCD_Module2.RST, A3.Pin_10
  N4: Nokia_5110_LCD_Module2.DC, A3.Pin_11
  N5: Nokia_5110_LCD_Module2.DIN, A3.Pin_16
  N6: Nokia_5110_LCD_Module2.CLK, A3.Pin_17
  N7: A2.Vcc#0, A3.Pin_1, A3.Pin_15, Sensor1.VCC, Sensor1.SIG, U1.+
  N8: A2.Vcc#1, A3.Pin_23
  N9: A2.Rx, A3.Pin_22

custom parts:
  Nokia 5110 LCD basado en PCD8544: Módulo Nokia 5110 LCD basado en el controlador PCD8544. Versión de 8 pines (sólo entrada).
  GY-NEO6MV2: Description: Module GPS , type GY-NEO6MV2, pour arduino et autres micro-contrôleurs. Caractéristiques De type GY-NEO6MV2 Alimentation 3V-5V Avec Flight Control EEPROM MWC Antenne large céramique, fort signal, 25 x 25 mm Paramètres de configuration sauvegardés en EEPROM Avec batterie de backup de données LED témoin de signal Module miniaturisé 25 x 35 mm Trou de fixation de 3mm Baud rate par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
  Waveshare rp2040-zero tht: .RP2040-Zero, A Low-Cost, High-Performance Pico-Like MCU Board Based On Raspberry Pi Microcontroller RP2040. This varant is THT without the extra connections.
  TTP223B Capacitive Touch Sensor Module: The TTP223B capacitive touch sensor module uses the TTP223B IC. The appropriate voltage is approximately 2 to 5.5 volts.
